# Fritzing sketch AR05_2LED (saved by Fritzing 0.9.3b)
breadboards: 1

parts:
  부품1 = Arduino Uno (Rev3)
  R1 = Resistor [tolerance=±5% resistance=220 package=THT]
  R2 = Resistor [tolerance=±5% resistance=220 package=THT]
  LED2 = LED - 5mm [color="Red (635nm)" package="5 mm [THT]"]
  LED3 = LED - 5mm [color="Green (555nm)" package="5 mm [THT]"]

nets:
  N1: 부품1.D3_PWM, LED2.anode
  N2: 부품1.GND, R1.Pin_1, R2.Pin_1
  N3: R1.Pin_0, LED3.cathode
  N4: R2.Pin_0, LED2.cathode
