# Fritzing sketch AR05_4LED (saved by Fritzing 0.9.3b)
breadboards: 1

parts:
  부품1 = Arduino Uno (Rev3)
  R1 = Resistor [tolerance=±5% resistance=220 package=THT]
  R2 = Resistor [tolerance=±5% resistance=220 package=THT]
  LED2 = LED - 5mm [color="Red (635nm)" package="5 mm [THT]"]
  LED3 = LED - 5mm [color="Green (555nm)" package="5 mm [THT]"]
  R3 = Resistor [tolerance=±5% resistance=220 package=THT]
  R4 = Resistor [tolerance=±5% resistance=220 package=THT]
  LED4 = LED - 5mm [color="Yellow (585nm)" package="5 mm [THT]"]
  LED5 = LED - 5mm [color="Blue (430nm)" package="5 mm [THT]"]

nets:
  N1: 부품1.D9_PWM, LED4.anode
  N2: 부품1.D3_PWM, LED2.anode
  N3: 부품1.D6_PWM, LED5.anode
  N4: 부품1.GND, R1.Pin_1, R2.Pin_1, R3.Pin_1, R4.Pin_1
  N5: R1.Pin_0, LED3.cathode
  N6: R2.Pin_0, LED2.cathode
  N7: R3.Pin_0, LED5.cathode
  N8: R4.Pin_0, LED4.cathode
